// Logisim project riscv.circ as structural Verilog: 11 circuits, main circuit alu
module alu (
  input  [31:0] A,
  input  [31:0] B,
  input  [3:0] alu_op_sel_i,
  output [31:0] D
);

  wire [31:0] adder_1_out, and_1_out, or_1_out, shifter_1_out, shifter_2_out, shifter_3_out,
       subtractor_1_out, xor_1_out;

  Adder #(.width(32)) adder_1 (.a(A), .b(B), .out(adder_1_out));  // open: cin, cout
  Subtractor #(.width(32)) subtractor_1 (.a(A), .b(B), .out(subtractor_1_out));  // open: bin, bout
  assign and_1_out = A & B;  // AND_Gate and_1, 32 bits wide
  assign or_1_out = A | B;  // OR_Gate or_1, 32 bits wide
  assign xor_1_out = A ^ B;  // XOR_Gate xor_1, 32 bits wide
  Shifter #(.shift("lr"), .width(32)) shifter_1 (.in(A), .\dist (B[4:0]), .out(shifter_1_out));
  Shifter #(.width(32)) shifter_2 (.in(A), .\dist (B[4:0]), .out(shifter_2_out));
  Shifter #(.shift("ar"), .width(32)) shifter_3 (.in(A), .\dist (B[4:0]), .out(shifter_3_out));
  Multiplexer #(.select(4), .width(32)) multiplexer_1 (
    .in0(adder_1_out), .in1(subtractor_1_out), .in2(and_1_out), .in3(or_1_out), .in4(xor_1_out),
    .in5(shifter_2_out), .in6(shifter_1_out), .in7(shifter_3_out), .in8(B), .in9({32{1'b0}}), .out(D),
    .sel(alu_op_sel_i));  // open: in10, in11, in12, in13, in14, in15

  // Other names for the same wires on the sheet: A_t[31:0] = A; B_t[31:0] = B; BL5_t[4:0] = B[4:0]
endmodule

module imm (
  input  [31:0] ins,
  input  [2:0] imm_sel_i,
  output [31:0] imm31_0
);

  wire [31:0] B, i, J, S;

  assign i = {{20{ins[31]}}, ins[31:20]};  // Bit_Extender bit_extender_1
  assign S = {{20{ins[31]}}, {ins[31:25], ins[11:7]}};  // Bit_Extender bit_extender_2
  assign B = {{19{ins[31]}}, {ins[31], ins[7], ins[30:25], ins[11:8], 1'b0}};  // Bit_Extender bit_extender_3
  assign J = {{11{ins[31]}}, {ins[31], ins[19:12], ins[20], ins[30:21], 1'b0}};  // Bit_Extender bit_extender_4
  Multiplexer #(.select(3), .width(32)) multiplexer_1 (
    .in0(i), .in1(S), .in2(B), .in3({ins[31:12], {12{1'b0}}}), .in4(J), .out(imm31_0), .sel(imm_sel_i));  // open: in5, in6, in7

  // Other names for the same wires on the sheet: ins_t[31:0] = ins; U[31:12] = ins[31:12]
endmodule

module regfile (
  input  r,
  input  [4:0] rdi,
  input  [31:0] rd,
  input  we,
  input  clk,
  input  [4:0] rsi1,
  input  [4:0] rsi2,
  output [31:0] rs1,
  output [31:0] rs2
);

  wire rt, we0_t, we1_t, we2_t, we3_t, we4_t, we5_t, we6_t, we7_t, we8_t, we9_t, we10_t, we11_t, we12_t,
       we13_t, we14_t, we15_t, we16_t, we17_t, we18_t, we19_t, we20_t, we21_t, we22_t, we23_t, we24_t,
       we25_t, we26_t, we27_t, we28_t, we29_t, we30_t, we31_t;
  wire [31:0] Q1_t, Q2_t, Q3_t, Q4_t, Q5_t, Q6_t, Q7_t, Q8_t, Q9_t, Q10_t, Q11_t, Q12_t, Q13_t, Q14_t, Q15_t,
       Q16_t, Q17_t, Q18_t, Q19_t, Q20_t, Q21_t, Q22_t, Q23_t, Q24_t, Q25_t, Q26_t, Q27_t, Q28_t, Q29_t,
       Q30_t, Q31_t;

  Demultiplexer #(.select(5)) demultiplexer_1 (
    .out0(we0_t), .out1(we1_t), .out2(we2_t), .out3(we3_t), .out4(we4_t), .out5(we5_t), .out6(we6_t),
    .out7(we7_t), .out8(we8_t), .out9(we9_t), .out10(we10_t), .out11(we11_t), .out12(we12_t), .out13(we13_t),
    .out14(we14_t), .out15(we15_t), .out16(we16_t), .out17(we17_t), .out18(we18_t), .out19(we19_t),
    .out20(we20_t), .out21(we21_t), .out22(we22_t), .out23(we23_t), .out24(we24_t), .out25(we25_t),
    .out26(we26_t), .out27(we27_t), .out28(we28_t), .out29(we29_t), .out30(we30_t), .out31(we31_t), .in(we),
    .sel(rdi));
  not not_1 (rt, r);
  Register #(.trigger("falling"), .width(32)) x4 (.D(rd), .en(we4_t), .clk(clk), .Q(Q4_t), .clr(rt));
  Register #(.trigger("falling"), .width(32)) x8 (.D(rd), .en(we8_t), .clk(clk), .Q(Q8_t), .clr(rt));
  Register #(.trigger("falling"), .width(32)) x12 (.D(rd), .en(we12_t), .clk(clk), .Q(Q12_t), .clr(rt));
  Register #(.trigger("falling"), .width(32)) x16 (.D(rd), .en(we16_t), .clk(clk), .Q(Q16_t), .clr(rt));
  Register #(.trigger("falling"), .width(32)) x20 (.D(rd), .en(we20_t), .clk(clk), .Q(Q20_t), .clr(rt));
  Register #(.trigger("falling"), .width(32)) x24 (.D(rd), .en(we24_t), .clk(clk), .Q(Q24_t), .clr(rt));
  Register #(.trigger("falling"), .width(32)) x28 (.D(rd), .en(we28_t), .clk(clk), .Q(Q28_t), .clr(rt));
  Register #(.trigger("falling"), .width(32)) x1 (.D(rd), .en(we1_t), .clk(clk), .Q(Q1_t), .clr(rt));
  Register #(.trigger("falling"), .width(32)) x5 (.D(rd), .en(we5_t), .clk(clk), .Q(Q5_t), .clr(rt));
  Register #(.trigger("falling"), .width(32)) x9 (.D(rd), .en(we9_t), .clk(clk), .Q(Q9_t), .clr(rt));
  Register #(.trigger("falling"), .width(32)) x13 (.D(rd), .en(we13_t), .clk(clk), .Q(Q13_t), .clr(rt));
  Register #(.trigger("falling"), .width(32)) x17 (.D(rd), .en(we17_t), .clk(clk), .Q(Q17_t), .clr(rt));
  Register #(.trigger("falling"), .width(32)) x21 (.D(rd), .en(we21_t), .clk(clk), .Q(Q21_t), .clr(rt));
  Register #(.trigger("falling"), .width(32)) x25 (.D(rd), .en(we25_t), .clk(clk), .Q(Q25_t), .clr(rt));
  Register #(.trigger("falling"), .width(32)) x29 (.D(rd), .en(we29_t), .clk(clk), .Q(Q29_t), .clr(rt));
  Register #(.trigger("falling"), .width(32)) x2 (.D(rd), .en(we2_t), .clk(clk), .Q(Q2_t), .clr(rt));
  Register #(.trigger("falling"), .width(32)) x6 (.D(rd), .en(we6_t), .clk(clk), .Q(Q6_t), .clr(rt));
  Register #(.trigger("falling"), .width(32)) x10 (.D(rd), .en(we10_t), .clk(clk), .Q(Q10_t), .clr(rt));
  Register #(.trigger("falling"), .width(32)) x14 (.D(rd), .en(we14_t), .clk(clk), .Q(Q14_t), .clr(rt));
  Register #(.trigger("falling"), .width(32)) x18 (.D(rd), .en(we18_t), .clk(clk), .Q(Q18_t), .clr(rt));
  Register #(.trigger("falling"), .width(32)) x22 (.D(rd), .en(we22_t), .clk(clk), .Q(Q22_t), .clr(rt));
  Register #(.trigger("falling"), .width(32)) x26 (.D(rd), .en(we26_t), .clk(clk), .Q(Q26_t), .clr(rt));
  Register #(.trigger("falling"), .width(32)) x30 (.D(rd), .en(we30_t), .clk(clk), .Q(Q30_t), .clr(rt));
  Register #(.trigger("falling"), .width(32)) x3 (.D(rd), .en(we3_t), .clk(clk), .Q(Q3_t), .clr(rt));
  Register #(.trigger("falling"), .width(32)) x7 (.D(rd), .en(we7_t), .clk(clk), .Q(Q7_t), .clr(rt));
  Register #(.trigger("falling"), .width(32)) x11 (.D(rd), .en(we11_t), .clk(clk), .Q(Q11_t), .clr(rt));
  Register #(.trigger("falling"), .width(32)) x15 (.D(rd), .en(we15_t), .clk(clk), .Q(Q15_t), .clr(rt));
  Register #(.trigger("falling"), .width(32)) x19 (.D(rd), .en(we19_t), .clk(clk), .Q(Q19_t), .clr(rt));
  Register #(.trigger("falling"), .width(32)) x23 (.D(rd), .en(we23_t), .clk(clk), .Q(Q23_t), .clr(rt));
  Register #(.trigger("falling"), .width(32)) x27 (.D(rd), .en(we27_t), .clk(clk), .Q(Q27_t), .clr(rt));
  Register #(.trigger("falling"), .width(32)) x31 (.D(rd), .en(we31_t), .clk(clk), .Q(Q31_t), .clr(rt));
  Multiplexer #(.select(5), .width(32)) multiplexer_1 (
    .in0({32{1'b0}}), .in1(Q1_t), .in2(Q2_t), .in3(Q3_t), .in4(Q4_t), .in5(Q5_t), .in6(Q6_t), .in7(Q7_t),
    .in8(Q8_t), .in9(Q9_t), .in10(Q10_t), .in11(Q11_t), .in12(Q12_t), .in13(Q13_t), .in14(Q14_t),
    .in15(Q15_t), .in16(Q16_t), .in17(Q17_t), .in18(Q18_t), .in19(Q19_t), .in20(Q20_t), .in21(Q21_t),
    .in22(Q22_t), .in23(Q23_t), .in24(Q24_t), .in25(Q25_t), .in26(Q26_t), .in27(Q27_t), .in28(Q28_t),
    .in29(Q29_t), .in30(Q30_t), .in31(Q31_t), .out(rs1), .sel(rsi1));
  Multiplexer #(.select(5), .width(32)) multiplexer_2 (
    .in0({32{1'b0}}), .in1(Q1_t), .in2(Q2_t), .in3(Q3_t), .in4(Q4_t), .in5(Q5_t), .in6(Q6_t), .in7(Q7_t),
    .in8(Q8_t), .in9(Q9_t), .in10(Q10_t), .in11(Q11_t), .in12(Q12_t), .in13(Q13_t), .in14(Q14_t),
    .in15(Q15_t), .in16(Q16_t), .in17(Q17_t), .in18(Q18_t), .in19(Q19_t), .in20(Q20_t), .in21(Q21_t),
    .in22(Q22_t), .in23(Q23_t), .in24(Q24_t), .in25(Q25_t), .in26(Q26_t), .in27(Q27_t), .in28(Q28_t),
    .in29(Q29_t), .in30(Q30_t), .in31(Q31_t), .out(rs2), .sel(rsi2));

  // Other names for the same wires on the sheet: clk_t = clk; rd_t[31:0] = rd; rdi_t[4:0] = rdi; we_t = we
endmodule

module comparatorunit (
  input  [31:0] port_a_i,
  input  [31:0] port_b_i,
  input  [2:0] comp_op_sel_i,
  output comp_o
);

  wire comparator_1_eq, comparator_2_lt, comparator_3_lt, not_1_out, not_2_out, not_3_out;

  Comparator #(.width(32)) comparator_1 (.a(port_a_i), .b(port_b_i), .eq(comparator_1_eq));  // open: gt, lt
  Comparator #(.width(32)) comparator_2 (.a(port_a_i), .b(port_b_i), .lt(comparator_2_lt));  // open: gt, eq
  Comparator #(.mode("unsigned"), .width(32)) comparator_3 (
    .a(port_a_i), .b(port_b_i), .lt(comparator_3_lt));  // open: gt, eq
  not not_1 (not_1_out, comparator_1_eq);
  not not_2 (not_2_out, comparator_2_lt);
  not not_3 (not_3_out, comparator_3_lt);
  Multiplexer #(.select(3)) multiplexer_1 (
    .in0(comparator_1_eq), .in1(not_1_out), .in2(comparator_2_lt), .in3(not_2_out), .in4(comparator_3_lt),
    .in5(not_3_out), .in6(1'b0), .out(comp_o), .sel(comp_op_sel_i));  // open: in7
endmodule

module loadstore (
  input  [3:0] load_store_type_i,
  input  [1:0] addr_offset_i,
  input  [31:0] read_data_i,
  input  [31:0] write_data_i,
  output [31:0] read_data_o,
  output [31:0] write_data_o,
  output [3:0] write_data_strobe_o
);

  wire [3:0] multiplexer_2_out, multiplexer_3_out;
  wire [7:0] multiplexer_5_out;
  wire [15:0] multiplexer_4_out;
  wire [31:0] bit_extender_1_out, bit_extender_2_out, bit_extender_3_out, bit_extender_4_out,
       bit_extender_5_out, bit_extender_6_out, bit_extender_7_out, bit_extender_8_out, multiplexer_1_out,
       multiplexer_6_out;

  assign bit_extender_1_out = {{16{1'b0}}, write_data_i[15:0]};  // Bit_Extender bit_extender_1
  assign bit_extender_2_out = {{24{1'b0}}, write_data_i[7:0]};  // Bit_Extender bit_extender_2
  Multiplexer #(.width(32)) multiplexer_1 (
    .in0(bit_extender_1_out), .in1({write_data_i[15:0], {16{1'b0}}}), .out(multiplexer_1_out),
    .sel(addr_offset_i[1]));
  assign bit_extender_3_out = {{16{1'b0}}, {write_data_i[7:0], {8{1'b0}}}};  // Bit_Extender bit_extender_3
  assign bit_extender_4_out = {{8{1'b0}}, {write_data_i[7:0], {16{1'b0}}}};  // Bit_Extender bit_extender_4
  Multiplexer #(.width(4)) multiplexer_2 (
    .in0(4'b0011), .in1(4'b1100), .out(multiplexer_2_out), .sel(addr_offset_i[1]));
  Multiplexer #(.select(2), .width(4)) multiplexer_3 (
    .in0(4'b0001), .in1(4'b0010), .in2(4'b0100), .in3(4'b1000), .out(multiplexer_3_out), .sel(addr_offset_i));
  Multiplexer #(.width(16)) multiplexer_4 (
    .in0(read_data_i[15:0]), .in1(read_data_i[31:16]), .out(multiplexer_4_out), .sel(addr_offset_i[1]));
  Multiplexer #(.select(2), .width(8)) multiplexer_5 (
    .in0(read_data_i[7:0]), .in1(read_data_i[15:8]), .in2(read_data_i[23:16]), .in3(read_data_i[31:24]),
    .out(multiplexer_5_out), .sel(addr_offset_i));
  Multiplexer #(.select(2), .width(32)) multiplexer_6 (
    .in0(bit_extender_2_out), .in1(bit_extender_3_out), .in2(bit_extender_4_out),
    .in3({write_data_i[7:0], {24{1'b0}}}), .out(multiplexer_6_out), .sel(addr_offset_i));
  assign bit_extender_5_out = {{16{multiplexer_4_out[15]}}, multiplexer_4_out};  // Bit_Extender bit_extender_5
  assign bit_extender_6_out = {{16{1'b0}}, multiplexer_4_out};  // Bit_Extender bit_extender_6
  assign bit_extender_7_out = {{24{multiplexer_5_out[7]}}, multiplexer_5_out};  // Bit_Extender bit_extender_7
  assign bit_extender_8_out = {{24{1'b0}}, multiplexer_5_out};  // Bit_Extender bit_extender_8
  Multiplexer #(.select(4), .width(4)) multiplexer_7 (
    .in5(4'b1111), .in6(multiplexer_2_out), .in7(multiplexer_3_out), .out(write_data_strobe_o),
    .sel(load_store_type_i));  // open: in0, in1, in2, in3, in4, in8, in9, in10, in11, in12, in13, in14, in15
  Multiplexer #(.select(4), .width(32)) multiplexer_8 (
    .in5(write_data_i), .in6(multiplexer_1_out), .in7(multiplexer_6_out), .out(write_data_o),
    .sel(load_store_type_i));  // open: in0, in1, in2, in3, in4, in8, in9, in10, in11, in12, in13, in14, in15
  Multiplexer #(.select(4), .width(32)) multiplexer_9 (
    .in0(read_data_i), .in1(bit_extender_5_out), .in2(bit_extender_6_out), .in3(bit_extender_7_out),
    .in4(bit_extender_8_out), .out(read_data_o), .sel(load_store_type_i));  // open: in5, in6, in7, in8, in9, in10, in11, in12, in13, in14, in15

  // Other names for the same wires on the sheet: addr_offset_i_t[1:0] = addr_offset_i;
  //   load_store_type_i_t[3:0] = load_store_type_i
endmodule

module pccounter (
  input  WE,
  input  clk,
  input  reset,
  input  [31:0] pc_target,
  input  next_pc_sel,
  output [31:0] outPCPlus4,
  output [31:0] outPC
);

  wire [31:0] multiplexer_1_out;

  Register #(.trigger("falling"), .width(32)) register_1 (
    .D(multiplexer_1_out), .en(WE), .clk(clk), .Q(outPC), .clr(reset));
  Adder #(.width(32)) adder_1 (.a(outPC), .b(32'h4), .out(outPCPlus4));  // open: cin, cout
  Multiplexer #(.width(32)) multiplexer_1 (
    .in0(outPCPlus4), .in1(pc_target), .out(multiplexer_1_out), .sel(next_pc_sel));
endmodule

module instructionmem (
  input  [31:0] addressinput,
  output [31:0] insout
);

  ROM #(.addrWidth(10), .dataWidth(32)) rom_1 (.addr(addressinput[11:2]), .data(insout));

  // Notes on the sheet:
  //   contents of rom_1 (hex, n*v repeats v):
  //   6400093 deadc137 eef10113 20a023 8183 108183 208183 308183 c183 10c183 20c183 30c183 9183 209183
  //   d183 20d183 13 13 13 6400193 2a00213 41a023 1a003 293 7*13
endmodule

module datamem (
  input  [3:0] write_mask,
  input  [31:0] addressinput,
  input  clk,
  input  [31:0] data_i,
  output [31:0] data_o
);

  wire or_1_out;

  or or_1 (or_1_out, write_mask[3], write_mask[2], write_mask[1], write_mask[0]);
  RAM #(.addrWidth(10), .asyncread("true"), .byteenables("byteEnables"), .dataWidth(32)) ram_1 (
    .addr(addressinput[11:2]), .we(or_1_out), .oe(1'b1), .clk(clk), .din(data_i), .dout(data_o),
    .be3(write_mask[3]), .be2(write_mask[2]), .be1(write_mask[1]), .be0(write_mask[0]));
endmodule

module writeback (
  input  [31:0] alu_result,
  input  [31:0] data_o,
  input  comp_result,
  input  [31:0] imm,
  input  [2:0] WBSel,
  input  [31:0] outPCPlus4,
  output [31:0] WBdata
);

  wire [31:0] bit_extender_1_out;

  assign bit_extender_1_out = {{31{1'b0}}, comp_result};  // Bit_Extender bit_extender_1
  Multiplexer #(.select(3), .width(32)) multiplexer_1 (
    .in0(alu_result), .in1(data_o), .in2(bit_extender_1_out), .in3(imm), .in4(outPCPlus4), .out(WBdata),
    .sel(WBSel));  // open: in5, in6, in7
endmodule

module processor (
  input  reset,
  input  mem_rbusy,
  input  is_mem_op,
  input  [2:0] in_4,
  input  [2:0] in_5,
  input  [2:0] in_6,
  input  [2:0] in_7,
  input  [2:0] in_8,
  input  [2:0] in_9,
  input  [2:0] in_10,
  input  [2:0] in_11,
  input  is_mem_write,
  input  mem_wbusy,
  input  [2:0] in_14,
  input  [2:0] in_15,
  input  [2:0] in_16,
  input  [2:0] in_17,
  input  [2:0] in_18,
  input  [31:0] in_19
);

  wire and_1_out, and_2_out, and_3_out, and_6_out, and_7_out, busy, clk_t, comp_o_t, comparator_1_eq,
       comparator_2_eq, comparator_3_eq, comparator_4_eq, comparator_8_eq, comparator_9_eq, comparator_10_eq,
       comparator_11_eq, comparator_12_eq, comparator_13_eq, comparator_14_eq, comparator_15_eq,
       corecontrolunit_1_comp_port_b_sel, corecontrolunit_1_data_memory_write, corecontrolunit_1_pc_mux_sel,
       corecontrolunit_1_port_a_sel, corecontrolunit_1_port_b_sel, corecontrolunit_1_reg_write_enable,
       execute_en, fetch_latch_en, func7b5_t, mem_done, mem_wait_en, not_1_out, not_2_out, not_3_out,
       not_4_out, not_5_out, not_6_out, not_7_out, not_8_out, or_1_out, or_3_out, or_4_out, or_5_out,
       writeback_en;
  wire [0:0] undriven;
  wire [2:0] corecontrolunit_1_comp_op_sel, corecontrolunit_1_imm_select,
       corecontrolunit_1_reg_write_data_sel, FSM_q, func3_t, multiplexer_1_out, multiplexer_2_out,
       multiplexer_3_out, state;
  wire [3:0] corecontrolunit_1_alu_op_sel, corecontrolunit_1_load_store_type,
       loadstore_1_write_data_strobe_o, multiplexer_12_out;
  wire [31:0] alu_o_t, currentPC, datamem_1_data_o, imm_t, ins_reg_out, instr, load_data_reg_q,
       loadstore_1_read_data_o, loadstore_1_write_data_o, multiplexer_4_out, multiplexer_8_out,
       multiplexer_9_out, multiplexer_10_out, multiplexer_11_out, pccounter_1_outpcplus4, rs1_t, rs2_t,
       writeback_1_wbdata;

  Clock clock_1 (.out(clk_t));
  Multiplexer #(.width(3)) multiplexer_1 (.in0(in_5), .in1(in_6), .out(multiplexer_1_out), .sel(mem_rbusy));
  Multiplexer #(.width(3)) multiplexer_2 (.in0(in_7), .in1(in_8), .out(multiplexer_2_out), .sel(comparator_1_eq));
  Comparator #(.width(7)) comparator_1 (.a(7'b0000011), .b(ins_reg_out[6:0]), .eq(comparator_1_eq));  // open: gt, lt
  Multiplexer #(.width(3)) multiplexer_3 (.in0(in_10), .in1(in_11), .out(multiplexer_3_out), .sel(busy));
  Register #(.width(3)) FSM (.D(state), .en(1'b1), .clk(clk_t), .Q(FSM_q), .clr(not_2_out));
  and and_1 (and_1_out, is_mem_write, mem_wbusy);
  not not_1 (not_1_out, is_mem_write);
  Multiplexer #(.width(32)) multiplexer_4 (.in0(in_19), .in1(instr), .out(multiplexer_4_out), .sel(reset));
  or or_1 (or_1_out, reset, fetch_latch_en);
  not not_2 (not_2_out, reset);
  Multiplexer #(.select(3), .width(3)) multiplexer_5 (
    .in0(in_4), .in1(multiplexer_1_out), .in2(multiplexer_2_out), .in3(multiplexer_3_out), .in4(in_9),
    .in5(in_9), .in6(in_9), .in7(in_9), .out(state), .sel(FSM_q));
  and and_2 (and_2_out, not_1_out, mem_rbusy);
  Comparator #(.width(3)) comparator_2 (.a(func3_t), .b(3'b001), .eq(comparator_2_eq));  // open: gt, lt
  Comparator #(.width(3)) comparator_3 (.a(func3_t), .b(3'b101), .eq(comparator_3_eq));  // open: gt, lt
  or or_2 (busy, and_1_out, and_2_out);
  Comparator #(.width(3)) comparator_4 (.a(state), .b(in_14), .eq(comparator_4_eq));  // open: gt, lt
  Comparator #(.width(3)) comparator_5 (.a(state), .b(in_15), .eq(execute_en));  // open: gt, lt
  Comparator #(.width(3)) comparator_6 (.a(state), .b(in_16), .eq(mem_wait_en));  // open: gt, lt
  Comparator #(.width(3)) comparator_7 (.a(state), .b(in_17), .eq(writeback_en));  // open: gt, lt
  Comparator #(.width(3)) comparator_8 (.a(state), .b(in_18), .eq(comparator_8_eq));  // open: gt, lt
  Comparator #(.width(7)) comparator_9 (.a(ins_reg_out[6:0]), .b(7'b0110011), .eq(comparator_9_eq));  // open: gt, lt
  Comparator #(.width(7)) comparator_10 (.a(ins_reg_out[6:0]), .b(7'b0010011), .eq(comparator_10_eq));  // open: gt, lt
  or or_3 (or_3_out, comparator_2_eq, comparator_3_eq);
  Register #(.width(32)) Instruction_Register (
    .D(multiplexer_4_out), .en(or_1_out), .clk(clk_t), .Q(ins_reg_out), .clr(not_3_out));
  not not_3 (not_3_out, reset);
  and and_3 (and_3_out, comparator_10_eq, or_3_out);
  not not_4 (not_4_out, mem_rbusy);
  not not_5 (not_5_out, busy);
  or or_4 (or_4_out, comparator_9_eq, and_3_out);
  Multiplexer multiplexer_6 (.in0(1'b0), .in1(ins_reg_out[30]), .out(func7b5_t), .sel(or_4_out));
  and and_4 (fetch_latch_en, comparator_4_eq, not_4_out);
  and and_5 (mem_done, comparator_8_eq, not_5_out);
  Comparator #(.width(7)) comparator_11 (.a(7'b0010111), .b(ins_reg_out[6:0]), .eq(comparator_11_eq));  // open: gt, lt
  Comparator #(.width(7)) comparator_12 (.a(7'b1101111), .b(ins_reg_out[6:0]), .eq(comparator_12_eq));  // open: gt, lt
  Comparator #(.width(7)) comparator_13 (.a(7'b0110111), .b(ins_reg_out[6:0]), .eq(comparator_13_eq));  // open: gt, lt
  or or_5 (or_5_out, comparator_11_eq, comparator_12_eq, comparator_13_eq);
  Multiplexer #(.width(3)) multiplexer_7 (.in0(ins_reg_out[14:12]), .in1(3'b000), .out(func3_t), .sel(or_5_out));
  Multiplexer #(.width(32)) multiplexer_8 (
    .in0(rs2_t), .in1(imm_t), .out(multiplexer_8_out), .sel(corecontrolunit_1_comp_port_b_sel));
  Multiplexer #(.width(32)) multiplexer_9 (
    .in0(currentPC), .in1(rs1_t), .out(multiplexer_9_out), .sel(corecontrolunit_1_port_a_sel));
  Multiplexer #(.width(32)) multiplexer_10 (
    .in0(imm_t), .in1(rs2_t), .out(multiplexer_10_out), .sel(corecontrolunit_1_port_b_sel));
  comparatorunit comparatorunit_1 (
    .port_a_i(rs1_t), .port_b_i(multiplexer_8_out), .comp_op_sel_i(corecontrolunit_1_comp_op_sel),
    .comp_o(comp_o_t));
  imm imm_1 (.ins(ins_reg_out), .imm_sel_i(corecontrolunit_1_imm_select), .imm31_0(imm_t));
  corecontrolunit corecontrolunit_1 (
    .branch_enable_i(comp_o_t), .opcode_i(ins_reg_out[6:0]), .func3_i(func3_t), .funct7_bit5_i(func7b5_t),
    .pc_mux_sel(corecontrolunit_1_pc_mux_sel), .port_b_sel(corecontrolunit_1_port_b_sel),
    .imm_select(corecontrolunit_1_imm_select), .alu_op_sel(corecontrolunit_1_alu_op_sel),
    .reg_write_data_sel(corecontrolunit_1_reg_write_data_sel),
    .load_store_type(corecontrolunit_1_load_store_type), .comp_op_sel(corecontrolunit_1_comp_op_sel),
    .comp_port_b_sel(corecontrolunit_1_comp_port_b_sel), .port_a_sel(corecontrolunit_1_port_a_sel),
    .reg_write_enable(corecontrolunit_1_reg_write_enable),
    .data_memory_write(corecontrolunit_1_data_memory_write));
  alu alu_1 (.A(multiplexer_9_out), .B(multiplexer_10_out), .alu_op_sel_i(corecontrolunit_1_alu_op_sel), .D(alu_o_t));
  not not_6 (not_6_out, reset);
  Comparator #(.width(7)) comparator_14 (.a(7'b1100111), .b(ins_reg_out[6:0]), .eq(comparator_14_eq));  // open: gt, lt
  Multiplexer #(.width(32)) multiplexer_11 (
    .in0(alu_o_t), .in1({alu_o_t[31:1], undriven[0]}), .out(multiplexer_11_out), .sel(comparator_14_eq));
  pccounter pccounter_1 (
    .WE(writeback_en), .clk(clk_t), .reset(not_6_out), .pc_target(multiplexer_11_out),
    .next_pc_sel(corecontrolunit_1_pc_mux_sel), .outPCPlus4(pccounter_1_outpcplus4), .outPC(currentPC));
  loadstore loadstore_1 (
    .load_store_type_i(corecontrolunit_1_load_store_type), .addr_offset_i(alu_o_t[1:0]),
    .read_data_i(datamem_1_data_o), .write_data_i(rs2_t), .read_data_o(loadstore_1_read_data_o),
    .write_data_o(loadstore_1_write_data_o), .write_data_strobe_o(loadstore_1_write_data_strobe_o));
  and and_6 (and_6_out, writeback_en, corecontrolunit_1_reg_write_enable);
  writeback writeback_1 (
    .alu_result(alu_o_t), .data_o(load_data_reg_q), .comp_result(comp_o_t), .imm(imm_t),
    .WBSel(corecontrolunit_1_reg_write_data_sel), .outPCPlus4(pccounter_1_outpcplus4),
    .WBdata(writeback_1_wbdata));
  Register #(.width(32)) load_data_reg (
    .D(loadstore_1_read_data_o), .en(mem_done), .clk(clk_t), .Q(load_data_reg_q), .clr(not_7_out));
  instructionmem instructionmem_1 (.addressinput(currentPC), .insout(instr));
  not not_7 (not_7_out, reset);
  Comparator #(.width(4)) comparator_15 (
    .a(loadstore_1_write_data_strobe_o), .b(4'b0000), .eq(comparator_15_eq));  // open: gt, lt
  regfile regfile_1 (
    .r(reset), .rdi(ins_reg_out[11:7]), .rd(writeback_1_wbdata), .we(and_6_out), .clk(clk_t),
    .rsi1(ins_reg_out[19:15]), .rsi2(ins_reg_out[24:20]), .rs1(rs1_t), .rs2(rs2_t));
  not not_8 (not_8_out, comparator_15_eq);
  and and_7 (and_7_out, corecontrolunit_1_data_memory_write, not_8_out);
  Multiplexer #(.width(4)) multiplexer_12 (
    .in0(4'b0000), .in1(loadstore_1_write_data_strobe_o), .out(multiplexer_12_out), .sel(and_7_out));
  datamem datamem_1 (
    .write_mask(multiplexer_12_out), .addressinput(alu_o_t), .clk(clk_t), .data_i(loadstore_1_write_data_o),
    .data_o(datamem_1_data_o));

  // Other names for the same wires on the sheet: opcode[6:0] = ins_reg_out[6:0]; rsi1_t[4:0] = ins_reg_out[19:15];
  //   rsi2_t[4:0] = ins_reg_out[24:20]; is_mem_op_t = is_mem_op; mem_rbusy_t = mem_rbusy; reset_t = reset

  // Notes on the sheet:
  //   in_19: initial=0x13
  //   in_4: initial=0x1
  //   in_14: initial=0x1
  //   in_15: initial=0x2
  //   in_16: initial=0x3
  //   in_17: initial=0x4
  //   in_18: initial=0x3
  //   in_10: initial=0x4
  //   in_11: initial=0x3
  //   in_5: initial=0x2
  //   in_6: initial=0x1
  //   in_7: initial=0x4
  //   in_8: initial=0x3
  //   0 for reset
  //   1 for normal working
  //   to check register files, go to regfile subcircuit
  //   to check memory, go to datamem subcircuit
  //    The reset pin is active low(0 means reset and 1 means normal working).   
  //   to load instructions, go to instructionmem subcircuit and load them in the ROM.
  //   when state=0 (FSM has D =0), instruction memory outputs the next instruction. 
  //   This processor is capable of executing all RV32I (Base Integer Instructions) except the 'ecall' and 'ebreak' instructions and has multicycle FSM control, with stages fetch, execute, memory wait, and writeback
endmodule

module corecontrolunit (
  input  branch_enable_i,
  input  [6:0] opcode_i,
  input  [2:0] func3_i,
  input  funct7_bit5_i,
  output pc_mux_sel,
  output port_b_sel,
  output [2:0] imm_select,
  output [3:0] alu_op_sel,
  output [2:0] reg_write_data_sel,
  output [3:0] load_store_type,
  output [2:0] comp_op_sel,
  output comp_port_b_sel,
  output port_a_sel,
  output reg_write_enable,
  output data_memory_write
);

  wire comparator_1_eq, comparator_2_eq, or_1_out;
  wire [23:0] rom_1_data;

  ROM #(.addrWidth(9), .dataWidth(24)) rom_1 (
    .addr({funct7_bit5_i, func3_i, opcode_i[6:2]}),
    .data({rom_1_data[23], reg_write_enable, imm_select, port_a_sel, port_b_sel, comp_port_b_sel, alu_op_sel, comp_op_sel, load_store_type, data_memory_write, reg_write_data_sel, rom_1_data[0]}));
  and and_1 (pc_mux_sel, rom_1_data[23], or_1_out);
  Comparator #(.width(7)) comparator_1 (.a(7'b1101111), .b(opcode_i), .eq(comparator_1_eq));  // open: gt, lt
  Comparator #(.width(7)) comparator_2 (.a(opcode_i), .b(7'b1100111), .eq(comparator_2_eq));  // open: gt, lt
  or or_1 (or_1_out, comparator_1_eq, comparator_2_eq, branch_enable_i);

  // Other names for the same wires on the sheet: opc[6:0] = opcode_i

  // Notes on the sheet:
  //   contents of rom_1 (hex, n*v repeats v):
  //   440c62 2c9d0a 2c9d0a 2c9d0a 450d00 580d00 2c9d0a 2c9d0a c0cfa 2c9d0a 2c9d0a 2c9d0a 6e0d00 588d00
  //   10*2c9d0a 90010a c40d08 2c9d0a e00d08 4*2c9d0a 440c22 2c9d0a 2c9d0a 2c9d0a 455d00 2c9d0a 2c9d0a
  //   2c9d0a c0cda 2c9d0a 2c9d0a 2c9d0a 6e5d00 11*2c9d0a 90030a 7*2c9d0a 440c02 2c9d0a 2c9d0a 2c9d0a
  //   459504 2c9d0a 2c9d0a 2c9d0a c0cba 2c9d0a 2c9d0a 2c9d0a 6e9504 23*2c9d0a 459904 7*2c9d0a 6e9904
  //   19*2c9d0a 440c82 2c9d0a 2c9d0a 2c9d0a 454d00 7*2c9d0a 6e4d00 11*2c9d0a 90050a 7*2c9d0a 440c42 2c9d0a
  //   2c9d0a 2c9d0a 456d00 7*2c9d0a 6e6d00 11*2c9d0a 90070a 11*2c9d0a 453d00 7*2c9d0a 6e3d00 11*2c9d0a
  //   90090a 11*2c9d0a 452d00 7*2c9d0a 6e2d00 11*2c9d0a 900b0a 19*2c9d0a 6e1d00 151*2c9d0a 457d00 7*2c9d0a
  //   6e7d00 83*2c9d0a
endmodule
